# Fritzing sketch Automated door system schematic (saved by Fritzing 0.9.3b)
circuit board: 8.46667cm x 5.64444cm

parts:
  Part1 = Arduino Mega 2560 (Rev3)
  J1 = Basic Servo
  hc-sr1 = hc-sr04

nets:
  GND: Part1.GND, J1.gnd, hc-sr1.GND
  N1: Part1.D12_PWM, hc-sr1.Trig
  N2: Part1.D11_PWM, hc-sr1.Echo
  N3: Part1.D9_PWM, J1.pulse
  VCC: Part1.5V, J1.vcc, hc-sr1.VCC

custom parts:
  Basic Servo: A generic servo.

// code stored in the sketch: Code in Fritzing.ino
#include <SR04.h>
#include <Servo.h>

//limz 2020
#include "SR04.h"
#define TRIG_PIN 12
#define ECHO_PIN 11

SR04 sr04 = SR04(ECHO_PIN,TRIG_PIN);
Servo door;
int pos = 0;    // variable to store the servo position
long a;

void setup() {
   Serial.begin(9600);
   delay(1000);
   door.attach(9);  // attaches the servo on pin 9 to the servo object
}

void loop() {
   /* a=sr04.Distance();
   Serial.print(a);
   Serial.println("cm");
   delay(1000); */

  a=sr04.Distance();
  
  if (a <= 50.0)
      { door.write(180); }
   else { door.write(0); }

    Serial.print(a) ;
    Serial.println("cm");


  /*for (pos = 0; pos <= 180; pos += 10) { // goes from 0 degrees to 180 degrees
    // in steps of 1 degree
    door.write(pos);              // tell servo to go to position in variable 'pos'
    delay(200);                       // waits 200ms for the servo to reach the position
  }
  
  for (pos = 180; pos >= 0; pos -= 10) { // goes from 180 degrees to 0 degrees
    door.write(pos);              // tell servo to go to position in variable 'pos'
    delay(200);                       // waits 200ms for the servo to reach the position
  }*/
}
